// Digital circuit blackjack.dig as structural Verilog
module blackjack (
  input  [9:0] in_1,
  input  [9:0] in_2,
  input  [3:0] in_3,
  input  in_6,
  input  in_7,
  input  in_8,
  input  in_9,
  input  in_10,
  input  in_11,
  input  in_12,
  output [9:0] out_4,
  output [9:0] out_5,
  output [6:0] out_13
);

  wire bussplitter_1_d0, bussplitter_1_d1, bussplitter_1_d2, bussplitter_1_d3, bussplitter_1_d4,
       bussplitter_1_d5, bussplitter_1_d6, bussplitter_2_d0, bussplitter_2_d1, bussplitter_2_d2,
       bussplitter_2_d3, bussplitter_2_d4, bussplitter_2_d5, bussplitter_2_d6, bussplitter_3_d0,
       bussplitter_3_d1, bussplitter_3_d2, bussplitter_3_d3, bussplitter_3_d4, bussplitter_3_d5,
       bussplitter_3_d6;
  wire [6:0] not_1_out, not_2_out, not_3_out, u_blackJack_hex0, u_blackJack_hex1, u_blackJack_hex2;

  blackJack #(.applicationType("GHDL"), .CodeFile("D:\\github\\uffs-arquivos\\SEM3\\sistemas-digitais\\TF\\blackjack.vhd")) u_blackJack (
    .KEY(in_1), .sw(in_2), .CLK(in_6), .card(in_3), .ledR(out_4), .ledG(out_5), .hex0(u_blackJack_hex0),
    .hex1(u_blackJack_hex1), .hex2(u_blackJack_hex2), .hex3(out_13));
  assign not_1_out = ~u_blackJack_hex2;  // Not not_1, 7 bits wide
  assign not_2_out = ~u_blackJack_hex0;  // Not not_2, 7 bits wide
  BusSplitter #(.Bits(7)) bussplitter_1 (
    .D(not_2_out), .OE(in_7), .D0(bussplitter_1_d0), .D1(bussplitter_1_d1), .D2(bussplitter_1_d2),
    .D3(bussplitter_1_d3), .D4(bussplitter_1_d4), .D5(bussplitter_1_d5), .D6(bussplitter_1_d6));
  BusSplitter #(.Bits(7)) bussplitter_2 (
    .D(not_1_out), .OE(in_11), .D0(bussplitter_2_d0), .D1(bussplitter_2_d1), .D2(bussplitter_2_d2),
    .D3(bussplitter_2_d3), .D4(bussplitter_2_d4), .D5(bussplitter_2_d5), .D6(bussplitter_2_d6));
  Seven_Seg seven_seg_1 (
    .a(bussplitter_1_d6), .b(bussplitter_1_d5), .c(bussplitter_1_d4), .d(bussplitter_1_d3),
    .e(bussplitter_1_d2), .f(bussplitter_1_d1), .g(bussplitter_1_d0), .dp(in_8));
  assign not_3_out = ~u_blackJack_hex1;  // Not not_3, 7 bits wide
  Seven_Seg seven_seg_2 (
    .a(bussplitter_2_d6), .b(bussplitter_2_d5), .c(bussplitter_2_d4), .d(bussplitter_2_d3),
    .e(bussplitter_2_d2), .f(bussplitter_2_d1), .g(bussplitter_2_d0), .dp(in_12));
  BusSplitter #(.Bits(7)) bussplitter_3 (
    .D(not_3_out), .OE(in_9), .D0(bussplitter_3_d0), .D1(bussplitter_3_d1), .D2(bussplitter_3_d2),
    .D3(bussplitter_3_d3), .D4(bussplitter_3_d4), .D5(bussplitter_3_d5), .D6(bussplitter_3_d6));
  Seven_Seg seven_seg_3 (
    .a(bussplitter_3_d6), .b(bussplitter_3_d5), .c(bussplitter_3_d4), .d(bussplitter_3_d3),
    .e(bussplitter_3_d2), .f(bussplitter_3_d1), .g(bussplitter_3_d0), .dp(in_10));

  // Notes on the sheet:
  //   in_1: default 1023
  //   in_7: default 1
  //   in_8: default 1
  //   in_9: default 1
  //   in_10: default 1
  //   in_11: default 1
  //   in_12: default 1
  //   VALOR DA CARTA
  //   NUMERO DO ESTADO 
  //   0 - START ...
  //   depois - pontuação
  //   NADA
  //   depois: pontuação
endmodule
