// Digital circuit processador8Bits.dig as structural Verilog
module processador8Bits (
  input  START,
  input  clk,
  output Terminado
);

  wire u_BR_CONTROLLER_id, u_BR_CONTROLLER_str, u_BR_CONTROLLER_value_in_select, u_BR_CONTROLLER_we,
       u_INST_MEM_CONTROLLER_id, u_INST_MEM_CONTROLLER_str, u_INST_MEM_CONTROLLER_valid_clk;
  wire [2:0] u_BR_CONTROLLER_a, u_BR_CONTROLLER_ra, u_BR_CONTROLLER_rb, u_BR_CONTROLLER_rw,
       u_INST_DECODER_inst_code, u_INST_DECODER_reg_a, u_INST_DECODER_reg_b, u_INST_DECODER_reg_dest;
  wire [4:0] u_INST_MEM_CONTROLLER_instruction_addrs;
  wire [7:0] multiplexer_1_out, ramdualport_2_d, registerfile_1_da, registerfile_1_db, u_BR_CONTROLLER_din,
       u_BR_CONTROLLER_ram, u_BR_CONTROLLER_ula_a, u_BR_CONTROLLER_ula_b, u_INST_DECODER_cnst, u_ULA_s;
  wire [11:0] ramdualport_1_d, u_INST_MEM_CONTROLLER_din;

  INST_MEM_CONTROLLER #(.applicationType("GHDL"), .CodeFile("D:\\github\\uffs-arquivos\\SEM4\\org\\processador8bits\\inst_mem_controller.vhd")) u_INST_MEM_CONTROLLER (
    .clk(clk), .start(START), .finalize(Terminado),
    .instruction_addrs(u_INST_MEM_CONTROLLER_instruction_addrs), .din(u_INST_MEM_CONTROLLER_din),
    .str(u_INST_MEM_CONTROLLER_str), .id(u_INST_MEM_CONTROLLER_id),
    .valid_clk(u_INST_MEM_CONTROLLER_valid_clk));
  RAMDualPort #(.AddrBits(5), .Bits(12)) ramdualport_1 (
    .A(u_INST_MEM_CONTROLLER_instruction_addrs), .Din(u_INST_MEM_CONTROLLER_din),
    .str(u_INST_MEM_CONTROLLER_str), .C(clk), .ld(u_INST_MEM_CONTROLLER_id), .D(ramdualport_1_d));
  INST_DECODER #(.applicationType("GHDL"), .CodeFile("D:\\github\\uffs-arquivos\\SEM4\\org\\processador8bits\\inst_decoder.vhd")) u_INST_DECODER (
    .operation(ramdualport_1_d), .reg_dest(u_INST_DECODER_reg_dest), .reg_a(u_INST_DECODER_reg_a),
    .reg_b(u_INST_DECODER_reg_b), .inst_code(u_INST_DECODER_inst_code), .cnst(u_INST_DECODER_cnst));
  Multiplexer #(.Bits(8)) multiplexer_1 (
    .sel(u_BR_CONTROLLER_value_in_select), .in_0(u_ULA_s), .in_1(ramdualport_2_d), .out(multiplexer_1_out));
  BR_CONTROLLER #(.applicationType("GHDL"), .CodeFile("D:\\github\\uffs-arquivos\\SEM4\\org\\processador8bits\\br_controller.vhd")) u_BR_CONTROLLER (
    .da(registerfile_1_da), .db(registerfile_1_db), .reg_dest(u_INST_DECODER_reg_dest),
    .reg_a(u_INST_DECODER_reg_a), .reg_b(u_INST_DECODER_reg_b), .inst(u_INST_DECODER_inst_code),
    .cnst(u_INST_DECODER_cnst), .value_in(multiplexer_1_out), .valid_clk(u_INST_MEM_CONTROLLER_valid_clk),
    .din(u_BR_CONTROLLER_din), .we(u_BR_CONTROLLER_we), .rw(u_BR_CONTROLLER_rw), .ra(u_BR_CONTROLLER_ra),
    .rb(u_BR_CONTROLLER_rb), .a(u_BR_CONTROLLER_a), .ram(u_BR_CONTROLLER_ram), .str(u_BR_CONTROLLER_str),
    .id(u_BR_CONTROLLER_id), .ula_a(u_BR_CONTROLLER_ula_a), .ula_b(u_BR_CONTROLLER_ula_b),
    .value_in_select(u_BR_CONTROLLER_value_in_select), .end_process(Terminado));
  RegisterFile #(.AddrBits(3), .Bits(8)) registerfile_1 (
    .Din(u_BR_CONTROLLER_din), .we(u_BR_CONTROLLER_we), .Rw(u_BR_CONTROLLER_rw), .C(clk),
    .Ra(u_BR_CONTROLLER_ra), .Rb(u_BR_CONTROLLER_rb), .Da(registerfile_1_da), .Db(registerfile_1_db));
  RAMDualPort #(.AddrBits(3), .isProgramMemory("true"), .Bits(8)) ramdualport_2 (
    .A(u_BR_CONTROLLER_a), .Din(u_BR_CONTROLLER_ram), .str(u_BR_CONTROLLER_str), .C(clk),
    .ld(u_BR_CONTROLLER_id), .D(ramdualport_2_d));
  ULA #(.applicationType("GHDL"), .CodeFile("D:\\github\\uffs-arquivos\\SEM4\\org\\processador8bits\\ula.vhd")) u_ULA (
    .a(u_BR_CONTROLLER_ula_a), .b(u_BR_CONTROLLER_ula_b), .op(u_INST_DECODER_inst_code), .s(u_ULA_s));

  // Notes on the sheet:
  //   Terminado: Terminado
  //   clk: Hz: 5
endmodule
